# Fritzing sketch Sketch JoyStick 7 segment control (saved by Fritzing 0.9.3b)
breadboards: 1

parts:
  LED1 = 7-SEGMENT-4DIGIT-YOUNGSUN [package=7-segment-4digit-youngsun-longpads]
  R2 = Resistor [tolerance=±5% resistance=1k package="2010 [SMD]"]
  R4 = Resistor [tolerance=±5% resistance=1k package="2010 [SMD]"]
  Part2 = Arduino Uno (Rev3) - ICSP
  Part1 = Thumb Joystick
  R5 = Resistor [tolerance=±5% resistance=1k package="2010 [SMD]"]
  R6 = Resistor [tolerance=±5% resistance=1k package="2010 [SMD]"]

nets:
  N1: LED1.DIG2, Part2.D2
  N2: LED1.D, Part2.D3_PWM
  N3: LED1.COL-A, Part2.D4
  N4: LED1.E, Part2.D5_PWM
  N5: LED1.DIG3, Part2.D6_PWM
  N6: LED1.DP, R2.Pin_0
  N7: LED1.APOS-A, Part2.D8
  N8: LED1.F, R6.Pin_0
  N9: LED1.COL-C, R5.Pin_0
  N10: LED1.C, Part2.ICSP_MOSI, Part2.D11_PWM/MOSI
  N11: LED1.A, Part2.D12/MISO
  N12: LED1.G, R4.Pin_1
  N13: R2.Pin_1, Part2.D7
  N14: R4.Pin_0, Part2.D13/SCK
  N15: Part2.A0, Part1.VERT
  N16: Part2.A1, Part1.HORZ
  N17: Part2.A2, Part1.SEL
  N18: Part2.D9_PWM, R6.Pin_1
  N19: Part2.D10_PWM/SS, R5.Pin_1
  5V: Part2.5V, Part1.VCC
  GND: Part2.GND, Part1.GND
